# Fritzing sketch DebitCardSystem (saved by Fritzing 0.9.9b)
circuit board: 4.2cm x 4.28654cm

parts:
  v1_0 = RFID-RC522-v2
  SSZ_DEBIT_CARD_SYSTEM = Arduino Nano (Rev3.0) (ICSP)
  HTTPS_//SSZ_CA = OLED 128x64 I2C Monochrome Display VDD-GND

nets:
  N1: v1_0.SDA, SSZ_DEBIT_CARD_SYSTEM.D10
  N2: v1_0.SCK, SSZ_DEBIT_CARD_SYSTEM.D13/SCK
  N3: v1_0.MOSI, SSZ_DEBIT_CARD_SYSTEM.D11/MOSI
  N4: v1_0.MISO, SSZ_DEBIT_CARD_SYSTEM.D12/MISO
  GND: v1_0.GND, SSZ_DEBIT_CARD_SYSTEM.GND, HTTPS_//SSZ_CA.GND
  N5: v1_0.RST, SSZ_DEBIT_CARD_SYSTEM.D9
  3.3V: v1_0.3.3V, SSZ_DEBIT_CARD_SYSTEM.3V3
  5V: SSZ_DEBIT_CARD_SYSTEM.5V, HTTPS_//SSZ_CA.VDD
  N6: SSZ_DEBIT_CARD_SYSTEM.A5, HTTPS_//SSZ_CA.SCK
  N7: SSZ_DEBIT_CARD_SYSTEM.A4, HTTPS_//SSZ_CA.SDA

custom parts:
  RFID-RC522-v2: A simple China made RFID-RC522 Reader; do check the pin labels, as this is a MFRC522 based clone.
  OLED 128x64 I2C Monochrome Display VDD-GND: OLED 128x64 I2C Monochrome Display. Note: there are two variants of this part, this one is the VDD GND SCK SDA variant. The other is GND VDD SCK SDA. Make sure you select the part that matches your module as using the incorrect part will probably destroy your module! In addition the mounting holes are marked on silkscreen but not by default drilled. If you want drilled mounting holes, copy a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

// code stored in the sketch: DebitCardSystem.ino
/*
This program is used along with the Unreal Engine app available at  https://ssz.ca/projectzero  to create a dedit card system
*/

#include <MFRC522.h>
#include <Adafruit_GFX.h>
#include <Adafruit_SSD1306.h>
#include <SPI.h>


Adafruit_SSD1306 display(4);

MFRC522 rfid(10, 9);
MFRC522::MIFARE_Key key; 

String UUIDString;

void setup() 
{
  Serial.begin(9600);
  SPI.begin();
  rfid.PCD_Init(); 
  display.begin(SSD1306_SWITCHCAPVCC, 0x3C);
  SetHomeScreen();
}

void loop() 
{
  if(  rfid.PICC_IsNewCardPresent())
  {
      ReadRFID();
  }
  delay(100);
}

void ReadRFID()
{
  rfid.PICC_ReadCardSerial();
  MFRC522::PICC_Type piccType = rfid.PICC_GetType(rfid.uid.sak);
  PrintDec(rfid.uid.uidByte, rfid.uid.size);
  UUIDString = String(rfid.uid.uidByte[0])+" "+String(rfid.uid.uidByte[1])+" "+String(rfid.uid.uidByte[2])+ " "+String(rfid.uid.uidByte[3]);
  PrintUID();
  rfid.PICC_HaltA();
  rfid.PCD_StopCrypto1();
}

void PrintDec(byte *buffer, byte bufferSize) 
{
  for (byte i = 0; i < bufferSize; i++) 
  {
    Serial.print(buffer[i] < 0x10 ? " 0" : " ");
    Serial.print(buffer[i], DEC);
  }
}

void PrintUID()
{
  display.clearDisplay();
  display.setTextColor(WHITE);
  display.setTextSize(1);
  display.setCursor(30,10); 
  display.print(UUIDString);
  display.setCursor(10,20); 
  display.print("CARD WAS SCANNED");
  display.display();
  delay(2000);
  SetHomeScreen();
}

void SetHomeScreen()
{
  display.clearDisplay();
  display.display();
  display.setTextColor(WHITE);
  display.setTextSize(2);
  display.setCursor(10,5); 
  display.print("SCAN CARD");
  display.display();
}
